# Fritzing sketch ESP_interrupt (saved by Fritzing 0.9.6b)

parts:
  U1 = ESP8266 NodeMCU LoLin module
  RHT1 = Humidity and Temperature Sensor RHT03

nets:
  N1: U1.D0, U1.RST
  3V3: U1.3V3, RHT1.Vcc
  N2: U1.GND, RHT1.GND_1
  N3: U1.D5, RHT1.Data-signal

notes:
  different pinouts exist
  Connect the DO pin to the RST pin only after uploading

custom parts:
  ESP8266 NodeMCU LoLin module: ESP8266 based NodeMCU
